# Fritzing sketch fritzing (saved by Fritzing 0.9.5d)
breadboards: 1

parts:
  Eris_Dev_Kit_v1_r1 = Eris Dev Kit v1 r2 [package=LQFP-48]
  DHT11_1 = DHT11 module
  KY-1 = Keyes Relay [package=THT]
  R1 = Photocell (LDR) [package=THT]
  Part1 = Soil Moisture Sensor
  Grove1 = Grove OLED 128x96

nets:
  N1: Eris_Dev_Kit_v1_r1.PA6, DHT11_1.DATA
  N2: Eris_Dev_Kit_v1_r1.PB0, R1.pin_1
  N3: Eris_Dev_Kit_v1_r1.PB1, Part1.SIG
  N4: Eris_Dev_Kit_v1_r1.PA7, KY-1.signal
  N5: Eris_Dev_Kit_v1_r1.PB8/SCL, Grove1.SCL
  N6: Eris_Dev_Kit_v1_r1.PB9/SDA, Grove1.SDA
  VCC: Eris_Dev_Kit_v1_r1.5V, DHT11_1.VCC, KY-1.power, Part1.VCC, Grove1.VCC
  GND: Eris_Dev_Kit_v1_r1.GND, DHT11_1.GND, KY-1.ground, R1.pin_0, Part1.GND, Grove1.GND

notes:
  RED - VCC
  BLACK - GROUND

custom parts:
  Eris Dev Kit v1 r2: Africa's Talking Eris Development Kit version 1 revision 2
  DHT11 module: DHT11 black pcb module
  Keyes Relay: The Keyes 5V relay module is suitable for SCM development, home appliance control. It uses a 5V~12V TIL control signal which can control DC / AC signal.
